// Logisim project atto-8.circ as structural Verilog: 1 circuit, main circuit main
module main (
);

  wire and_1_out, and_4_out, and_5_out, button_1_out, CIN, CLK, CLR_SC, counter_2_carry, counter_3_carry,
       COUT, COUT_CF, DATA_AL, DATA_IL, DATA_IP, DATA_MEM, DATA_SP, DATA_XL, DATA_YL, DATA_ZL, DISPLAY,
       IP_DATA, keyboard_1_avail, MEM_DATA, multiplexer_1_out, NAND_DATA, not_1_out, not_2_out, not_3_out,
       not_4_out, not_5_out, not_6_out, not_7_out, not_8_out, not_10_out, OFST_AND_CF, OFST_DATA, ONES_DATA,
       or_1_out, or_2_out, or_3_out, or_4_out, RESET, s_r_ff_1_q, s_r_ff_1_qn, SIZE_AND_CIN, SIZE_DATA,
       SP_DATA, STDIN, STDOUT, SUM_DATA, ZERO, ZERO_CF;
  wire [3:0] demultiplexer_2_out0, register_8_q;
  wire [4:0] counter_1_q, counter_2_q, undriven;
  wire [5:5] register_7_q;
  wire [6:0] keyboard_1_data;
  wire [7:0] adder_1_out, ADDR, button_2_out, DATA, demultiplexer_1_out0, demultiplexer_1_out1,
       demultiplexer_1_out2, demultiplexer_1_out3, demultiplexer_1_out4, demultiplexer_1_out5,
       demultiplexer_1_out6, demultiplexer_1_out7, demultiplexer_1_out8, demultiplexer_1_out9,
       demultiplexer_1_out10, demultiplexer_1_out11, demultiplexer_1_out12, demultiplexer_1_out13,
       demultiplexer_1_out14, demultiplexer_1_out15, demultiplexer_1_out16, demultiplexer_1_out17,
       demultiplexer_1_out18, demultiplexer_1_out19, demultiplexer_1_out20, demultiplexer_1_out21,
       demultiplexer_1_out22, demultiplexer_1_out23, demultiplexer_1_out24, demultiplexer_1_out25,
       demultiplexer_1_out26, demultiplexer_1_out27, demultiplexer_1_out28, demultiplexer_1_out29,
       demultiplexer_1_out30, demultiplexer_1_out31, MEMADDR, MEMDATA, multiplexer_2_out, nand_1_out,
       or_5_out, pull_resistor_1_node, register_1_q, register_2_q, register_3_q, register_4_q, register_5_q,
       ROM0_data;
  wire [7:4] register_8_q_2;
  wire [7:7] not_9_out;
  wire [8:0] counter_3_q, undriven_2;

  not not_1 (not_1_out, STDIN);
  Register register_1 (.D(DATA), .en(DATA_XL), .clk(CLK), .Q(register_1_q), .clr(RESET));
  LedBar ledbar_1 (
    .led0(register_1_q[7]), .led1(register_1_q[6]), .led2(register_1_q[5]), .led3(register_1_q[4]),
    .led4(register_1_q[3]), .led5(register_1_q[2]), .led6(register_1_q[1]), .led7(register_1_q[0]));
  Register register_2 (.D(DATA), .en(DATA_YL), .clk(CLK), .Q(register_2_q), .clr(RESET));
  LedBar ledbar_2 (
    .led0(register_2_q[7]), .led1(register_2_q[6]), .led2(register_2_q[5]), .led3(register_2_q[4]),
    .led4(register_2_q[3]), .led5(register_2_q[2]), .led6(register_2_q[1]), .led7(register_2_q[0]));
  Register register_3 (.D(DATA), .en(DATA_ZL), .clk(CLK), .Q(register_3_q), .clr(RESET));
  LedBar ledbar_3 (
    .led0(register_3_q[7]), .led1(register_3_q[6]), .led2(register_3_q[5]), .led3(register_3_q[4]),
    .led4(register_3_q[3]), .led5(register_3_q[2]), .led6(register_3_q[1]), .led7(register_3_q[0]));
  Register register_4 (.D(DATA), .en(DATA_IP), .clk(CLK), .Q(register_4_q), .clr(RESET));
  LedBar ledbar_4 (
    .led0(register_4_q[7]), .led1(register_4_q[6]), .led2(register_4_q[5]), .led3(register_4_q[4]),
    .led4(register_4_q[3]), .led5(register_4_q[2]), .led6(register_4_q[1]), .led7(register_4_q[0]));
  Register register_5 (.D(DATA), .en(DATA_SP), .clk(CLK), .Q(register_5_q), .clr(RESET));
  LedBar ledbar_5 (
    .led0(register_5_q[7]), .led1(register_5_q[6]), .led2(register_5_q[5]), .led3(register_5_q[4]),
    .led4(register_5_q[3]), .led5(register_5_q[2]), .led6(register_5_q[1]), .led7(register_5_q[0]));
  Register register_6 (.D(DATA), .en(DATA_AL), .clk(CLK), .Q(ADDR), .clr(RESET));
  LedBar ledbar_6 (
    .led0(ADDR[7]), .led1(ADDR[6]), .led2(ADDR[5]), .led3(ADDR[4]), .led4(ADDR[3]), .led5(ADDR[2]),
    .led6(ADDR[1]), .led7(ADDR[0]));
  and and_1 (and_1_out, MEM_DATA, not_1_out);
  Counter #(.max('h1f), .width(5)) counter_1 (
    .clr(RESET), .load(1'b0), .up(1'b1), .count(DISPLAY), .clk(not_2_out), .D(undriven), .Q(counter_1_q));  // open: carry
  not not_2 (not_2_out, CLK);
  // NoConnect on undriven
  RAM #(.asyncread("true"), .databus("bidir")) MEM (
    .addr(MEMADDR), .we(or_1_out), .oe(or_2_out), .clk(CLK), .data(MEMDATA));
  or or_1 (or_1_out, DATA_MEM, RESET);
  or or_2 (or_2_out, and_1_out, DISPLAY);
  nor nor_1 (STDOUT, ADDR[0], ADDR[1], ADDR[2], ADDR[3], ADDR[4], ADDR[5], ADDR[6], ADDR[7]);
  S_R_Flip_Flop s_r_ff_1 (
    .S(STDOUT), .R(1'b0), .clk(not_3_out), .Q(s_r_ff_1_q), .reset(RESET), .Qn(s_r_ff_1_qn), .preset(1'b0));
  not not_3 (not_3_out, MEM_DATA);
  Adder adder_1 (.a(register_1_q), .b(register_2_q), .out(adder_1_out), .cin(CIN), .cout(COUT));
  assign nand_1_out = ~(register_2_q & register_3_q);  // NAND_Gate nand_1, 8 bits wide
  nor nor_2 (ZERO, nand_1_out[0], nand_1_out[1], nand_1_out[2], nand_1_out[3], nand_1_out[4], nand_1_out[5], nand_1_out[6], nand_1_out[7]);
  assign DATA = IP_DATA ? register_4_q : 8'bz;  // Controlled_Buffer controlled_buffer_1
  assign DATA = SP_DATA ? register_5_q : 8'bz;  // Controlled_Buffer controlled_buffer_2
  assign MEMADDR = MEM_DATA ? ADDR : 8'bz;  // Controlled_Buffer controlled_buffer_3
  and and_2 (STDIN, STDOUT, s_r_ff_1_q);
  // NoConnect on s_r_ff_1_qn
  LedBar ledbar_7 (
    .led0(adder_1_out[7]), .led1(adder_1_out[6]), .led2(adder_1_out[5]), .led3(adder_1_out[4]),
    .led4(adder_1_out[3]), .led5(adder_1_out[2]), .led6(adder_1_out[1]), .led7(adder_1_out[0]));
  LedBar ledbar_8 (
    .led0(nand_1_out[7]), .led1(nand_1_out[6]), .led2(nand_1_out[5]), .led3(nand_1_out[4]),
    .led4(nand_1_out[3]), .led5(nand_1_out[2]), .led6(nand_1_out[1]), .led7(nand_1_out[0]));
  LedBar ledbar_9 (
    .led0(1'b1), .led1(1'b1), .led2(1'b1), .led3(1'b1), .led4(1'b1), .led5(1'b1), .led6(1'b1), .led7(1'b1));
  assign MEMADDR = DATA_MEM ? ADDR : 8'bz;  // Controlled_Buffer controlled_buffer_4
  assign MEMADDR = DISPLAY ? {3'b111, counter_1_q} : 8'bz;  // Controlled_Buffer controlled_buffer_5
  assign DATA = SUM_DATA ? adder_1_out : 8'bz;  // Controlled_Buffer controlled_buffer_6
  assign DATA = NAND_DATA ? nand_1_out : 8'bz;  // Controlled_Buffer controlled_buffer_7
  assign DATA = ONES_DATA ? {8{1'b1}} : 8'bz;  // Controlled_Buffer controlled_buffer_8
  assign DATA = MEM_DATA ? MEMDATA : 8'bz;  // Controlled_Buffer controlled_buffer_9
  LedBar ledbar_10 (
    .led0(DATA[7]), .led1(DATA[6]), .led2(DATA[5]), .led3(DATA[4]), .led4(DATA[3]), .led5(DATA[2]),
    .led6(DATA[1]), .led7(DATA[0]));
  assign DATA = OFST_DATA ? {4'b0000, register_8_q} : 8'bz;  // Controlled_Buffer controlled_buffer_10
  assign DATA = SIZE_DATA ? {4'b0000, demultiplexer_2_out0} : 8'bz;  // Controlled_Buffer controlled_buffer_11
  assign MEMDATA = DATA_MEM ? DATA : 8'bz;  // Controlled_Buffer controlled_buffer_12
  Pull_Resistor pull_resistor_1 (.node(pull_resistor_1_node));
  assign pull_resistor_1_node = DISPLAY ? MEMDATA : 8'bz;  // Controlled_Buffer controlled_buffer_13
  Demultiplexer #(.enable("true"), .select(5), .width(8)) demultiplexer_1 (
    .out0(demultiplexer_1_out0), .out1(demultiplexer_1_out1), .out2(demultiplexer_1_out2),
    .out3(demultiplexer_1_out3), .out4(demultiplexer_1_out4), .out5(demultiplexer_1_out5),
    .out6(demultiplexer_1_out6), .out7(demultiplexer_1_out7), .out8(demultiplexer_1_out8),
    .out9(demultiplexer_1_out9), .out10(demultiplexer_1_out10), .out11(demultiplexer_1_out11),
    .out12(demultiplexer_1_out12), .out13(demultiplexer_1_out13), .out14(demultiplexer_1_out14),
    .out15(demultiplexer_1_out15), .out16(demultiplexer_1_out16), .out17(demultiplexer_1_out17),
    .out18(demultiplexer_1_out18), .out19(demultiplexer_1_out19), .out20(demultiplexer_1_out20),
    .out21(demultiplexer_1_out21), .out22(demultiplexer_1_out22), .out23(demultiplexer_1_out23),
    .out24(demultiplexer_1_out24), .out25(demultiplexer_1_out25), .out26(demultiplexer_1_out26),
    .out27(demultiplexer_1_out27), .out28(demultiplexer_1_out28), .out29(demultiplexer_1_out29),
    .out30(demultiplexer_1_out30), .out31(demultiplexer_1_out31), .in(pull_resistor_1_node),
    .sel(counter_1_q), .en(CLK));
  Counter #(.max('h1f), .width(5)) counter_2 (
    .clr(or_3_out), .load(1'b0), .up(1'b1), .count(not_4_out), .clk(not_5_out), .carry(counter_2_carry),
    .Q(counter_2_q));  // open: D
  or or_3 (or_3_out, RESET, CLR_SC);
  not not_4 (not_4_out, RESET);
  not not_5 (not_5_out, CLK);
  Multiplexer multiplexer_1 (.in0(COUT), .in1(ZERO), .out(multiplexer_1_out), .sel(ZERO_CF));
  Demultiplexer #(.select(2)) demultiplexer_2 (
    .out0(demultiplexer_2_out0[0]), .out1(demultiplexer_2_out0[1]), .out2(demultiplexer_2_out0[2]),
    .out3(demultiplexer_2_out0[3]), .in(1'b1), .sel(register_8_q[1:0]));
  not not_6 (not_6_out, RESET);
  not not_7 (not_7_out, MEM_DATA);
  not not_8 (not_8_out, DATA_MEM);
  LedBar #(.matrixcols(5)) ledbar_11 (
    .led0(counter_2_q[4]), .led1(counter_2_q[3]), .led2(counter_2_q[2]), .led3(counter_2_q[1]),
    .led4(counter_2_q[0]));
  Register #(.width(1)) register_7 (.D(multiplexer_1_out), .en(or_4_out), .clk(CLK), .Q(register_7_q[5]), .clr(RESET));
  or or_4 (or_4_out, ZERO_CF, COUT_CF);
  Register register_8 (.D(DATA), .en(DATA_IL), .clk(CLK), .Q({register_8_q_2, register_8_q}), .clr(RESET));
  LedBar ledbar_12 (
    .led0(register_8_q_2[7]), .led1(register_8_q_2[6]), .led2(register_8_q_2[5]), .led3(register_8_q_2[4]),
    .led4(register_8_q[3]), .led5(register_8_q[2]), .led6(register_8_q[1]), .led7(register_8_q[0]));
  and and_3 (DISPLAY, not_6_out, not_7_out, not_8_out);
  DotMatrix #(.inputtype("row"), .matrixcols(8), .matrixrows(8), .persist(96)) dotmatrix_1 (
    .row0(demultiplexer_1_out0), .row1(demultiplexer_1_out2), .row2(demultiplexer_1_out4),
    .row3(demultiplexer_1_out6), .row4(demultiplexer_1_out8), .row5(demultiplexer_1_out10),
    .row6(demultiplexer_1_out12), .row7(demultiplexer_1_out14));
  DotMatrix #(.inputtype("row"), .matrixcols(8), .matrixrows(8), .persist(96)) dotmatrix_2 (
    .row0(demultiplexer_1_out16), .row1(demultiplexer_1_out18), .row2(demultiplexer_1_out20),
    .row3(demultiplexer_1_out22), .row4(demultiplexer_1_out24), .row5(demultiplexer_1_out26),
    .row6(demultiplexer_1_out28), .row7(demultiplexer_1_out30));
  // NoConnect on counter_2_carry
  LedBar #(.matrixcols(1)) ledbar_13 (.led0(register_7_q[5]));
  not not_9 (not_9_out[7], register_8_q_2[7]);
  Clock #(.phaseOffset(1)) clock_1 (.out(CLK));
  Button button_1 (.out(button_1_out));
  not not_10 (not_10_out, CLK);
  // DotMatrix #(.inputtype("row"), .matrixcols(8), .matrixrows(8), .persist(96)) dotmatrix_3: pin names not known; wires that end beside it: demultiplexer_1_out1, demultiplexer_1_out3, demultiplexer_1_out5, demultiplexer_1_out7, demultiplexer_1_out9
  // DotMatrix #(.inputtype("row"), .matrixcols(8), .matrixrows(8), .persist(96)) dotmatrix_4: pin names not known; wires that end beside it: demultiplexer_1_out11, demultiplexer_1_out13, demultiplexer_1_out15, demultiplexer_1_out17, demultiplexer_1_out19, demultiplexer_1_out21, demultiplexer_1_out23, demultiplexer_1_out25, demultiplexer_1_out27, demultiplexer_1_out29, demultiplexer_1_out31
  // NoConnect on or_5_out[7]
  assign or_5_out = {{4{not_9_out[7]}}, 4'b0000} | {register_8_q_2, register_8_q};  // OR_Gate or_5, 8 bits wide
  Counter #(.max('h1ff), .width(9)) counter_3 (
    .clr(button_1_out), .load(1'b0), .up(1'b1), .count(RESET), .clk(not_10_out), .D(undriven_2),
    .carry(counter_3_carry), .Q(counter_3_q));
  // NoConnect on undriven_2
  ROM #(.addrWidth(13), .dataWidth(16)) MIC (
    .addr({or_5_out[6:0], register_7_q[5], counter_2_q}),
    .data({CLR_SC, DATA_IL, SIZE_AND_CIN, OFST_AND_CF, IP_DATA, DATA_IP, SP_DATA, DATA_SP, DATA_AL, MEM_DATA, DATA_MEM, DATA_XL, DATA_YL, DATA_ZL, SUM_DATA, NAND_DATA}));
  // NoConnect on counter_3_carry
  assign MEMADDR = RESET ? counter_3_q[7:0] : 8'bz;  // Controlled_Buffer controlled_buffer_14
  ROM ROM0 (.addr(counter_3_q[7:0]), .data(ROM0_data));
  not not_11 (RESET, counter_3_q[8]);
  // NoConnect on DATA[7]
  TTY tty_1 (.data(DATA[6:0]), .clk(CLK), .we(and_4_out), .clr(RESET));
  and and_4 (and_4_out, STDOUT, DATA_MEM);
  Keyboard #(.buflen(256)) keyboard_1 (
    .clk(CLK), .re(and_5_out), .clr(RESET), .avail(keyboard_1_avail), .data(keyboard_1_data));
  and and_5 (and_5_out, MEM_DATA, STDIN);
  Demultiplexer #(.select(2)) demultiplexer_3 (
    .out0(OFST_DATA), .out1(COUT_CF), .out2(ZERO_CF), .in(OFST_AND_CF), .sel({NAND_DATA, SUM_DATA}));  // open: out3
  Demultiplexer demultiplexer_4 (.out0(SIZE_DATA), .out1(CIN), .in(SIZE_AND_CIN), .sel(SUM_DATA));
  Button button_2 (.out(button_2_out[0]));
  Button button_3 (.out(button_2_out[3]));
  Button button_4 (.out(button_2_out[2]));
  Button button_5 (.out(button_2_out[1]));
  LedBar #(.matrixcols(16)) ledbar_14 (
    .led0(NAND_DATA), .led1(SUM_DATA), .led2(DATA_ZL), .led3(DATA_YL), .led4(DATA_XL), .led5(DATA_MEM),
    .led6(MEM_DATA), .led7(DATA_AL), .led8(DATA_SP), .led9(SP_DATA), .led10(DATA_IP), .led11(IP_DATA),
    .led12(OFST_AND_CF), .led13(SIZE_AND_CIN), .led14(DATA_IL), .led15(CLR_SC));
  nor nor_3 (ONES_DATA, SIZE_DATA, OFST_DATA, IP_DATA, SP_DATA, SUM_DATA, NAND_DATA, MEM_DATA);
  Button button_6 (.out(button_2_out[4]));
  Button button_7 (.out(button_2_out[7]));
  Button button_8 (.out(button_2_out[6]));
  Button button_9 (.out(button_2_out[5]));
  assign MEMDATA = RESET ? ROM0_data : 8'bz;  // Controlled_Buffer controlled_buffer_15
  Multiplexer #(.width(8)) multiplexer_2 (
    .in0(button_2_out), .in1({1'b0, keyboard_1_data}), .out(multiplexer_2_out), .sel(keyboard_1_avail));
  assign MEMDATA = and_5_out ? multiplexer_2_out : 8'bz;  // Controlled_Buffer controlled_buffer_16

  // Other names for the same wires on the sheet: WRT = DATA_MEM; READ = MEM_DATA; RST = RESET; SET_CIN = CIN

  // Notes on the sheet:
  //   XL
  //   YL
  //   ZL
  //   IP
  //   SP
  //   AL
  //   SUM
  //   NAND
  //   ONES
  //   MEM
  //   ADDR
  //   DATA
  //   IL
  //   SC
  //   CF
  //   OFST
  //   SIZE
  //   . . . . . . . . . . . . . . . . . . . . . . . . . . . . . . . . . . . . . . . . . . . . . . . . . . . . . . . . . . . . . . . . . . . . . . . . . . . . . . . . . . . . . . . . . . . . . . . . . . . . . . . . . . . . . . . . . . . . . . . . . . . . . . . . . . . . . . . . . . . . . . . . . . . . . . . . . . . . . . . . . . . . . . . . 
  //   CLK
  //   RST
  //   DISPLAY
  //   MIC
  //   Atto-8 Microprocessor
  //   Atto-8 Microcomputer
  //   CTRL
  //   STDIO
endmodule
